// Digital circuit 4-bit-adder.dig as structural Verilog
module _4_bit_adder (
  input  [3:0] A,
  input  [3:0] B,
  output Sum,
  output Overflow_Flag
);

  wire _1_bit_adder_1_sum, _1_bit_adder_2_carry_out, _1_bit_adder_2_sum, _1_bit_adder_3_carry_out,
       _1_bit_adder_3_sum, _1_bit_adder_4_carry_out;

  _1_bit_adder _1_bit_adder_1 (
    .A(A[3]), .B(B[3]), .Carry_in(_1_bit_adder_2_carry_out), .Sum(_1_bit_adder_1_sum),
    .Carry_out(Overflow_Flag));
  _1_bit_adder _1_bit_adder_2 (
    .A(A[2]), .B(B[2]), .Carry_in(_1_bit_adder_3_carry_out), .Sum(_1_bit_adder_2_sum),
    .Carry_out(_1_bit_adder_2_carry_out));
  _1_bit_adder _1_bit_adder_3 (
    .A(A[1]), .B(B[1]), .Carry_in(_1_bit_adder_4_carry_out), .Sum(_1_bit_adder_3_sum),
    .Carry_out(_1_bit_adder_3_carry_out));
  _1_bit_adder _1_bit_adder_4 (.A(A[0]), .B(B[0]), .Carry_in(1'b0), .Sum(Sum), .Carry_out(_1_bit_adder_4_carry_out));
endmodule
