// Digital circuit part 1-2-3.dig as structural Verilog
module part_1_2_3 (
  input  A,
  input  B,
  input  C,
  input  A_2,
  input  B_2,
  input  C_2,
  input  A_3,
  input  B_3,
  input  C_3,
  input  D,
  input  A1,
  input  A0,
  input  B1,
  input  B0,
  output out_4,
  output out_8,
  output out_13,
  output out_18,
  output out_19,
  output out_20,
  output out_21
);

  wire and_2_out, and_4_out, and_5_out, and_6_out, and_8_out;

  and and_1 (out_4, A, B, C);
  and and_2 (and_2_out, A_2, B_2);
  nand nand_1 (out_13, A_3, B_3, C_3, D);
  or or_1 (out_8, and_2_out, C_2);
  and and_3 (out_18, A0, B0);
  and and_4 (and_4_out, A1, B0);
  and and_5 (and_5_out, A1, B1);
  and and_6 (and_6_out, A0, B1);
  and and_7 (out_21, A1, B1, A0, B0);
  and and_8 (and_8_out, A0, B1);
  xor xor_1 (out_20, and_5_out, and_6_out);
  xor xor_2 (out_19, and_8_out, and_4_out);
endmodule
